# Fritzing sketch VU_Meter (saved by Fritzing 0.9.3b)
breadboards: 1

parts:
  YwRobot_Power_Supply1 = YwRobot Breadboard Power Supply [part_number=545043]  # not connected
  Bauteil1 = Arduino Micro (Rev3)  # not connected
  R1 = Resistor [tolerance=±5% resistance=10k package=THT]
  C1 = Electrolytic Capacitor [capacitance=10µF package="100 mil [THT, electrolytic]"]
  R2 = Resistor [tolerance=±5% resistance=10k package=THT]
  U1 = WS2812 RGB LED matrix 8x8
  TRS1 = SUYIN Audio Jack (TRS) 3.5mm [package="SUYIN [THT]"]
  Bauteil2 = Arduino Pro Mini v13  # not connected
  Bauteil3 = Arduino Nano (Rev3.0)

nets:
  VCC: R1.Pin_0, U1.VCC, Bauteil3.5V
  N1: R1.Pin_1, C1.-, R2.Pin_1, Bauteil3.A5
  N2: C1.+, TRS1.Ring
  N3: R2.Pin_0, U1.GND
  N4: U1.DIN, Bauteil3.D13/SCK
  N5: TRS1.Sleeve, Bauteil3.GND

custom parts:
  YwRobot Breadboard Power Supply: The YwRobot Breadboard Power Supply (MB-V2) has two power rails; they can be 5V or 3V3. Power to the module can be provided through the female USB socket or through the A10 (female) 2.1mm power jack.
  WS2812 RGB LED matrix 8x8: WS2812 matrix 8x8
  SUYIN Audio Jack (TRS) 3.5mm: Stereo Jack 3.5mm
