# Fritzing sketch VU_Meter_Teil 3 (saved by Fritzing 0.9.3b)
breadboards: 2

parts:
  R1 = Resistor [tolerance=±5% resistance=10k package=THT]
  C1 = Electrolytic Capacitor [capacitance=10µF package="100 mil [THT, electrolytic]"]
  R2 = Resistor [tolerance=±5% resistance=10k package=THT]
  U1 = WS2812 RGB LED matrix 8x8
  TRS1 = SUYIN Audio Jack (TRS) 3.5mm [package="SUYIN [THT]"]
  Bauteil3 = Arduino Nano (Rev3.0)
  C2 = Electrolytic Capacitor [capacitance=10µF package="100 mil [THT, electrolytic]"]
  R4 = Resistor [tolerance=±5% resistance=10k package=THT]
  R5 = Resistor [tolerance=±5% resistance=10k package=THT]
  D1 = Zener Diode [part_number=1N4732A breakdown_voltage=5.1V package="Melf DO-213 AB [SMD]"]
  D2 = Zener Diode [part_number=1N4732A breakdown_voltage=5.1V package="Melf DO-213 AB [SMD]"]
  R8 = Resistor [tolerance=±1% resistance=100 package="0603 [SMD]"]
  R9 = Resistor [tolerance=±1% resistance=100 package="0603 [SMD]"]
  U3 = POT [package=pot_mammoth]
  R14 = Trimmer Potentiometer [maximum_resistance=5kΩ package=THT]
  R16 = Trimmer Potentiometer [maximum_resistance=5kΩ package=THT]
  U6 = POT [package=pot_mammoth]

nets:
  VCC: R1.Pin_0, U1.VCC, Bauteil3.5V, R5.Pin_0, U3.E, U6.S
  N1: R1.Pin_1, C1.-, R2.Pin_1, Bauteil3.A5, D1.cathode
  N2: C1.+, R8.Pin_0
  GND: R2.Pin_0, U1.GND, TRS1.Sleeve, Bauteil3.GND, R4.Pin_0, D1.anode, D2.anode, U3.S, U6.E
  N3: U1.DIN, Bauteil3.D13/SCK
  N4: Bauteil3.A4, C2.-, R4.Pin_1, R5.Pin_1, D2.cathode
  N5: Bauteil3.A3, U3.A
  N6: Bauteil3.A2, U6.A
  N7: C2.+, R9.Pin_0
  N8: R8.Pin_1, R14.wiper
  N9: R9.Pin_1, R16.wiper
  N10: R14.leg1, R14.leg2
  N11: R16.leg1, R16.leg2

custom parts:
  WS2812 RGB LED matrix 8x8: WS2812 matrix 8x8
  SUYIN Audio Jack (TRS) 3.5mm: Stereo Jack 3.5mm
